# Fritzing sketch Testing (saved by Fritzing 0.9.2b)
breadboards: 1

parts:
  Part1 = Arduino Uno (Rev3)
  R1 = Resistor [tolerance=±5% resistance=47k package=THT]
  R2 = Slide Potentiometer [maximum_resistance=250kΩ]
  S1 = Toggle Switch [package=THT]
  R3 = Resistor [tolerance=±5% resistance=47k package=THT]
  R5 = Resistor [tolerance=±5% resistance=47k package=THT]
  R7 = Resistor [tolerance=±5% resistance=47k package=THT]
  S2 = Toggle Switch [package=THT]
  R4 = Slide Potentiometer [maximum_resistance=250kΩ]
  S3 = Toggle Switch [package=THT]
  R6 = Slide Potentiometer [maximum_resistance=250kΩ]
  S4 = Toggle Switch [package=THT]
  R8 = Slide Potentiometer [maximum_resistance=250kΩ]

nets:
  N1: Part1.A0, R1.Pin_0, R2.leg2
  N2: Part1.A1, R3.Pin_0, R4.leg2
  N3: Part1.A2, R5.Pin_0, R6.leg2
  N4: Part1.A3, R7.Pin_0, R8.leg2
  5V: Part1.5V, S1.COM, S2.COM, S3.COM, S4.COM
  GND: Part1.GND, R1.Pin_1, R3.Pin_1, R5.Pin_1, R7.Pin_1
  N5: R2.wiper, S1.L2
  N6: S2.L2, R4.wiper
  N7: S3.L2, R6.wiper
  N8: S4.L2, R8.wiper
